// Logisim project 4-Floor Elavator Control System.circ as structural Verilog: 1 circuit, main circuit main
module main (
  input  F3,
  input  F2,
  input  F1,
  input  F0,
  input  En,
  input  Reset
);

  wire and_1_out, and_2_out, and_3_out, and_4_out, and_5_out, and_6_out, and_7_out, and_8_out, and_9_out,
       and_10_out, and_11_out, and_12_out, and_13_out, and_14_out, and_15_out, and_16_out, CLK_out, d_ff_1_q,
       d_ff_2_q, d_ff_5_q, d_ff_6_q, decoder_1_out0, decoder_1_out1, decoder_1_out2, decoder_1_out3,
       or_1_out, or_2_out, or_3_out, or_4_out, or_5_out, or_6_out, or_7_out, or_8_out, or_9_out,
       priority_encoder_1_gs;
  wire [1:0] d_ff_3_q, priority_encoder_1_out;

  Clock CLK (.out(CLK_out));
  and and_1 (and_1_out, ~d_ff_6_q, ~d_ff_5_q, ~d_ff_3_q[1], ~d_ff_1_q, d_ff_2_q);  // AND_Gate
  and and_2 (and_2_out, ~d_ff_6_q, ~d_ff_5_q, d_ff_3_q[1], d_ff_1_q, d_ff_2_q);  // AND_Gate
  and and_3 (and_3_out, d_ff_6_q, d_ff_3_q[1], ~d_ff_3_q[0]);  // AND_Gate
  and and_4 (and_4_out, d_ff_3_q[1], ~d_ff_3_q[0], d_ff_2_q);  // AND_Gate
  and and_5 (and_5_out, ~d_ff_6_q, ~d_ff_5_q, d_ff_3_q[0], d_ff_1_q);  // AND_Gate
  and and_6 (and_6_out, d_ff_5_q, ~d_ff_3_q[1], d_ff_3_q[0]);  // AND_Gate
  and and_7 (and_7_out, ~d_ff_6_q, d_ff_3_q[1], ~d_ff_3_q[0], d_ff_1_q);  // AND_Gate
  and and_8 (and_8_out, ~d_ff_6_q, d_ff_5_q, d_ff_3_q[1], ~d_ff_3_q[0]);  // AND_Gate
  and and_9 (and_9_out, ~d_ff_6_q, ~d_ff_5_q, d_ff_3_q[1], d_ff_3_q[0], ~d_ff_1_q, ~d_ff_2_q);  // AND_Gate
  and and_10 (and_10_out, ~d_ff_6_q, ~d_ff_5_q, ~d_ff_3_q[1], d_ff_1_q, d_ff_2_q);  // AND_Gate
  and and_11 (and_11_out, d_ff_6_q, d_ff_5_q, ~d_ff_3_q[1], d_ff_3_q[0]);  // AND_Gate
  and and_12 (and_12_out, ~d_ff_6_q, ~d_ff_5_q, ~d_ff_3_q[1], ~d_ff_3_q[0], d_ff_1_q);  // AND_Gate
  and and_13 (and_13_out, ~d_ff_6_q, ~d_ff_5_q, ~d_ff_3_q[1], ~d_ff_3_q[0], d_ff_1_q, d_ff_2_q);  // AND_Gate
  and and_14 (and_14_out, ~d_ff_6_q, ~d_ff_5_q, d_ff_3_q[1], ~d_ff_3_q[0], ~d_ff_1_q, ~d_ff_2_q);  // AND_Gate
  and and_15 (and_15_out, d_ff_6_q, d_ff_5_q, d_ff_3_q[1], ~d_ff_3_q[0]);  // AND_Gate
  and and_16 (and_16_out, ~d_ff_6_q, ~d_ff_5_q, d_ff_3_q[1], d_ff_3_q[0], ~d_ff_1_q);  // AND_Gate
  Pull_Resistor pull_resistor_1 (.node(priority_encoder_1_out[1]));
  Priority_Encoder #(.select(2), .disabled(0)) priority_encoder_1 (
    .in0(F0), .in1(F1), .in2(F2), .in3(F3), .out(priority_encoder_1_out), .gs(priority_encoder_1_gs),
    .en_in(En));  // open: en_out
  Pull_Resistor pull_resistor_2 (.node(priority_encoder_1_out[0]));
  or or_1 (or_1_out, and_14_out, and_1_out, and_2_out, and_12_out, and_3_out, and_8_out, and_4_out);
  or or_2 (or_2_out, and_16_out, and_5_out, and_6_out, and_7_out, and_8_out);
  or or_3 (or_3_out, and_9_out, and_10_out, and_11_out, and_12_out);
  or or_4 (or_4_out, and_13_out, and_14_out, and_15_out, and_16_out);
  D_Flip_Flop #(.trigger("high")) d_ff_1 (
    .clk(priority_encoder_1_gs), .D(priority_encoder_1_out[1]), .Q(d_ff_1_q), .en(En), .reset(Reset));  // open: Qn, preset
  D_Flip_Flop #(.trigger("high")) d_ff_2 (
    .clk(priority_encoder_1_gs), .D(priority_encoder_1_out[0]), .Q(d_ff_2_q), .en(En), .reset(Reset));  // open: Qn, preset
  Decoder #(.select(2), .enable("false")) decoder_1 (
    .out0(decoder_1_out0), .out1(decoder_1_out1), .out2(decoder_1_out2), .out3(decoder_1_out3), .sel(d_ff_3_q));
  D_Flip_Flop d_ff_3 (.clk(CLK_out), .D(or_1_out), .Q(d_ff_3_q[0]), .en(En), .reset(Reset));  // open: Qn, preset
  D_Flip_Flop d_ff_4 (.clk(CLK_out), .D(or_2_out), .Q(d_ff_3_q[1]), .en(En), .reset(Reset));  // open: Qn, preset
  D_Flip_Flop d_ff_5 (.clk(CLK_out), .D(or_3_out), .Q(d_ff_5_q), .en(En), .reset(Reset));  // open: Qn, preset
  D_Flip_Flop d_ff_6 (.clk(CLK_out), .D(or_4_out), .Q(d_ff_6_q), .en(En), .reset(Reset));  // open: Qn, preset
  LED u_F3 (.in(decoder_1_out3));
  LED u_F2 (.in(decoder_1_out2));
  LED u_F1 (.in(decoder_1_out1));
  LED u_F0 (.in(decoder_1_out0));
  or or_5 (or_5_out, decoder_1_out2, decoder_1_out1);
  or or_6 (or_6_out, decoder_1_out3, decoder_1_out2, decoder_1_out1, decoder_1_out0);
  or or_7 (or_7_out, decoder_1_out3, decoder_1_out2, decoder_1_out0);
  or or_8 (or_8_out, decoder_1_out2, decoder_1_out1);
  or or_9 (or_9_out, decoder_1_out3, decoder_1_out2, decoder_1_out1);
  _7_Segment_Display u_7_segment_display_1 (
    .g(or_9_out), .f(decoder_1_out3), .a(or_5_out), .b(or_6_out), .e(decoder_1_out1), .d(or_8_out),
    .c(or_7_out));  // open: dp

  // Notes on the sheet:
  //   D1 = Q3'Q2'Q1Q0B' + Q3'Q2'Q0B + Q2Q1'Q0 + Q3'Q1Q0'B + Q3'Q2Q1Q0'
  //   D2 = Q3'Q2'Q1Q0B'A' + Q3'Q2'Q1'BA + Q3Q2Q1'Q0 + Q3'Q2'Q1'Q0'B
  //   D3 = Q3'Q2'Q1'Q0'BA + Q3'Q2'Q1Q0'B'A' + Q3Q2Q1Q0' + Q3'Q2'Q1Q0B'
  //   D0 = Q3'Q2'Q1Q0'B'A' + Q3'Q2'Q1'B'A + Q3'Q2'Q1BA + Q3'Q2'Q1'Q0'B + Q3Q1Q0' + Q3'Q2Q1Q0' + Q1Q0'A
endmodule
